// Logisim project test.circ as structural Verilog: 1 circuit, main circuit main
module main (
  input  [3:0] in_1,
  input  in_2,
  input  in_3,
  input  in_4,
  input  in_5,
  input  b,
  input  a,
  input  cin,
  output out_9,
  output out_10,
  output out_11,
  output out_12,
  output out_13
);

  wire and_1_out, and_2_out, xor_3_out;

  or or_1 (out_12, and_1_out, and_2_out);
  and and_1 (and_1_out, a, b);
  xor xor_1 (out_10, in_2, in_3);
  Adder #(.width(1)) adder_1 (.a(in_4), .b(in_5), .out(out_11));  // open: cin, cout
  and and_2 (and_2_out, a, xor_3_out);
  xor xor_2 (out_13, a, xor_3_out);
  xor xor_3 (xor_3_out, a, b);

  assign cin = a;
endmodule
